// Logisim project cpu_with_pipeline.circ as structural Verilog: 13 circuits, main circuit main
module main (
);

  wire clk, control_1_alusrc, control_1_bneorbeq, control_1_branch, control_1_memread, control_1_memtoreg,
       control_1_memwrite, control_1_readrs, control_1_readrt, control_1_regwrite,
       pipeline_id_ex_1_memreadex, pipeline_id_ex_1_memtoregex, pipeline_id_ex_1_memwriteex,
       pipeline_id_ex_1_regwriteex, RegDst, ZeroExtend;
  wire [3:0] multiplexer_1_out, pipeline_id_ex_1_writeregex, undriven;
  wire [15:0] adder_1_out, extender_immediate_1_output, PC_q, pipeline_id_ex_1_r1ex, pipeline_id_ex_1_r2ex,
       pipeline_if_id_1_instid, pipeline_if_id_1_pcplus4if, regfile_1_r1, regfile_1_r2, rom_1_data,
       undriven_2;

  Register #(.width(16)) PC (.Q(PC_q), .clk(clk));  // open: D, en, clr
  Clock clock_1 (.out(clk));
  Adder #(.width(16)) adder_1 (.a(PC_q), .b(16'h4), .out(adder_1_out));  // open: cin, cout
  ROM #(.dataWidth(16)) rom_1 (.addr(PC_q[9:2]), .data(rom_1_data));  // open: sel
  pipeline_IF_ID pipeline_if_id_1 (
    .InstIF(rom_1_data), .PCPlus4ID(adder_1_out), .InstID(pipeline_if_id_1_instid),
    .PCPlus4IF(pipeline_if_id_1_pcplus4if), .clk(clk));  // open: En, clr
  Control control_1 (
    .op(pipeline_if_id_1_instid[15:12]), .MemRead(control_1_memread), .MemWrite(control_1_memwrite),
    .ALUSrc(control_1_alusrc), .MemtoReg(control_1_memtoreg), .Branch(control_1_branch), .RegDst(RegDst),
    .RegWrite(control_1_regwrite), .BneOrBeq(control_1_bneorbeq), .ReadRs(control_1_readrs),
    .ZeroExtend(ZeroExtend), .ReadRt(control_1_readrt));
  Multiplexer #(.width(4), .enable("false")) multiplexer_1 (
    .in0(pipeline_if_id_1_instid[7:4]), .out(multiplexer_1_out), .sel(RegDst));  // open: in1
  Extender_immediate extender_immediate_1 (
    .Input(pipeline_if_id_1_instid[7:0]), .Output(extender_immediate_1_output), .ZeroExtend(ZeroExtend));
  RegFile regfile_1 (
    .R1_num(pipeline_if_id_1_instid[11:8]), .R2_num(pipeline_if_id_1_instid[7:4]), .RW(undriven),
    .Din(undriven_2), .R1(regfile_1_r1), .R2(regfile_1_r2));  // open: WE, clk
  pipeline_ID_EX pipeline_id_ex_1 (
    .MemReadID(control_1_memread), .ImmID(extender_immediate_1_output), .MemWriteID(control_1_memwrite),
    .R1ID(regfile_1_r1), .ALUSrcID(control_1_alusrc), .R2ID(regfile_1_r2), .MemtoRegID(control_1_memtoreg),
    .PCPlus4ID(pipeline_if_id_1_pcplus4if), .BranchID(control_1_branch), .WriteRegID(multiplexer_1_out),
    .RegWriteID(control_1_regwrite), .BneOrBeqID(control_1_bneorbeq), .MemReadEX(pipeline_id_ex_1_memreadex),
    .MemWriteEX(pipeline_id_ex_1_memwriteex), .R1EX(pipeline_id_ex_1_r1ex), .R2EX(pipeline_id_ex_1_r2ex),
    .MemtoRegEX(pipeline_id_ex_1_memtoregex), .WriteRegEX(pipeline_id_ex_1_writeregex),
    .RegWriteEX(pipeline_id_ex_1_regwriteex), .clk(clk), .En(1'b1));  // open: ImmEX, ALUSrcEX, PCPlusEX, BranchEX, BneOrBeqEX, clr
  pipeline_EX_MEM pipeline_ex_mem_1 (
    .MemReadEX(pipeline_id_ex_1_memreadex), .MemWriteEX(pipeline_id_ex_1_memwriteex),
    .MemtoRegEX(pipeline_id_ex_1_memtoregex), .RegWriteEX(pipeline_id_ex_1_regwriteex),
    .WriteRegEX(pipeline_id_ex_1_writeregex), .clk(clk));  // open: ALUResultEX, WriteDataEX, ALUResultMEM, MemReadMEM, WriteDataMEM, MemWriteMEM, MemtoRegMEM, RegWriteMEM, WriteRegMEM, clr, En

  // Notes on the sheet:
  //   PCPlus4IF
  //   OP
  //   Ignore
  //   RS
  //   RT
  //   RD
endmodule

module hazard_detector (
  input  op0,
  input  op1,
  input  op2,
  input  op3,
  output ReadRs,
  output ReadRt
);

  wire and_1_out, and_2_out, and_3_out, and_4_out, and_5_out, and_6_out, and_7_out, and_8_out, and_9_out,
       and_10_out, and_11_out, and_12_out, and_13_out, and_14_out, not_1_out, not_2_out, not_3_out,
       not_4_out, not_5_out, not_6_out, not_7_out, not_8_out, not_9_out, not_10_out, not_11_out, not_12_out,
       not_13_out, not_14_out, not_15_out, not_16_out, not_17_out, not_18_out, not_19_out, not_20_out,
       not_21_out, not_22_out, not_23_out, not_24_out, not_25_out, not_26_out, not_27_out, not_28_out,
       not_29_out, not_30_out, not_31_out, not_32_out, not_33_out, not_34_out, not_35_out, not_36_out,
       not_37_out, not_38_out, not_39_out, not_40_out, not_41_out;

  not not_1 (not_1_out, op0);
  not not_2 (not_2_out, op1);
  not not_3 (not_3_out, op2);
  not not_4 (not_4_out, op3);
  not not_5 (not_5_out, op0);
  not not_6 (not_6_out, op1);
  not not_7 (not_7_out, op3);
  not not_8 (not_8_out, op0);
  not not_9 (not_9_out, op1);
  not not_10 (not_10_out, op3);
  not not_11 (not_11_out, op0);
  not not_12 (not_12_out, op1);
  not not_13 (not_13_out, op0);
  not not_14 (not_14_out, op1);
  not not_15 (not_15_out, op1);
  not not_16 (not_16_out, op2);
  not not_17 (not_17_out, op3);
  not not_18 (not_18_out, op1);
  not not_19 (not_19_out, op3);
  not not_20 (not_20_out, op0);
  not not_21 (not_21_out, op1);
  not not_22 (not_22_out, op2);
  not not_23 (not_23_out, op0);
  not not_24 (not_24_out, op1);
  not not_25 (not_25_out, op2);
  not not_26 (not_26_out, op0);
  not not_27 (not_27_out, op1);
  not not_28 (not_28_out, op3);
  not not_29 (not_29_out, op0);
  not not_30 (not_30_out, op1);
  not not_31 (not_31_out, op2);
  not not_32 (not_32_out, op3);
  not not_33 (not_33_out, op0);
  not not_34 (not_34_out, op1);
  not not_35 (not_35_out, op2);
  not not_36 (not_36_out, op0);
  not not_37 (not_37_out, op1);
  not not_38 (not_38_out, op2);
  not not_39 (not_39_out, op0);
  not not_40 (not_40_out, op2);
  not not_41 (not_41_out, op3);
  and and_1 (and_1_out, not_11_out, not_12_out, op2, op3);
  and and_2 (and_2_out, not_13_out, not_14_out, op2, op3);
  and and_3 (and_3_out, op0, not_15_out, not_16_out, not_17_out);
  and and_4 (and_4_out, op0, not_18_out, op2, not_19_out);
  and and_5 (and_5_out, not_1_out, not_2_out, not_3_out, not_4_out);
  and and_6 (and_6_out, not_5_out, not_6_out, op2, not_7_out);
  and and_7 (and_7_out, not_8_out, not_9_out, op2, not_10_out);
  and and_8 (and_8_out, not_20_out, not_21_out, not_22_out, op3);
  and and_9 (and_9_out, not_23_out, not_24_out, not_25_out, op3);
  and and_10 (and_10_out, not_26_out, not_27_out, op2, not_28_out);
  and and_11 (and_11_out, not_29_out, not_30_out, not_31_out, not_32_out);
  and and_12 (and_12_out, not_33_out, not_34_out, not_35_out, op3);
  and and_13 (and_13_out, not_36_out, not_37_out, not_38_out, op3);
  and and_14 (and_14_out, not_39_out, op1, not_40_out, not_41_out);
  or or_1 (ReadRs, and_5_out, and_6_out, and_7_out, and_1_out, and_2_out, and_3_out, and_4_out, and_8_out, and_9_out, and_10_out);
  or or_2 (ReadRt, and_11_out, and_12_out, and_13_out, and_14_out);
endmodule

module hazard_unit (
  input  ReadRs,
  input  ReadRt,
  input  [3:0] RT,
  input  [3:0] RS,
  input  RegWriteMEM,
  input  [3:0] WriteReg_MEM,
  input  RegWriteEX,
  input  [3:0] WriteReg_EX,
  input  clk,
  input  IsToBranchOrJump,
  output FlushID,
  output StallIF,
  output StallID,
  output FlushIF
);

  wire and_1_out, and_2_out, and_3_out, and_4_out, and_6_out, and_7_out, and_8_out, and_9_out,
       comparator_1_eq, comparator_2_eq, comparator_3_eq, comparator_4_eq, comparator_5_eq, comparator_6_eq,
       d_ff_1_q, d_ff_2_q, not_1_out, not_2_out, or_1_out, or_2_out;

  not not_1 (not_1_out, comparator_1_eq);
  Comparator #(.width(4)) comparator_1 (.a(4'b0000), .b(WriteReg_MEM), .eq(comparator_1_eq));  // open: gt, lt
  Comparator #(.width(4)) comparator_2 (.a(WriteReg_MEM), .b(RT), .eq(comparator_2_eq));  // open: gt, lt
  Comparator #(.width(4)) comparator_3 (.a(WriteReg_MEM), .b(RS), .eq(comparator_3_eq));  // open: gt, lt
  Comparator #(.width(4)) comparator_4 (.a(4'b0000), .b(WriteReg_EX), .eq(comparator_4_eq));  // open: gt, lt
  not not_2 (not_2_out, comparator_4_eq);
  Comparator #(.width(4)) comparator_5 (.a(WriteReg_EX), .b(RT), .eq(comparator_5_eq));  // open: gt, lt
  Comparator #(.width(4)) comparator_6 (.a(WriteReg_EX), .b(RS), .eq(comparator_6_eq));  // open: gt, lt
  and and_1 (and_1_out, comparator_5_eq, ReadRt);
  and and_2 (and_2_out, comparator_6_eq, ReadRs);
  and and_3 (and_3_out, comparator_2_eq, ReadRt);
  or or_1 (or_1_out, and_3_out, and_4_out);
  and and_4 (and_4_out, comparator_3_eq, ReadRs);
  or or_2 (or_2_out, and_1_out, and_2_out);
  and and_5 (FlushIF, ~clk, d_ff_1_q);  // AND_Gate
  D_Flip_Flop #(.trigger("falling")) d_ff_1 (
    .clk(clk), .D(IsToBranchOrJump), .Q(d_ff_1_q));  // open: Qn, preset, en, reset
  and and_6 (and_6_out, not_1_out, or_1_out);
  and and_7 (and_7_out, not_2_out, or_2_out);
  and and_8 (and_8_out, RegWriteMEM, and_6_out);
  and and_9 (and_9_out, RegWriteEX, and_7_out);
  or or_3 (StallID, and_8_out, and_9_out);
  and and_10 (FlushID, clk, d_ff_2_q);
  D_Flip_Flop #(.trigger("falling")) d_ff_2 (.clk(clk), .D(StallID), .Q(d_ff_2_q));  // open: Qn, preset, en, reset

  assign StallIF = StallID;
endmodule

module ALU (
  input  [3:0] AluOP,
  input  [15:0] Y,
  input  [15:0] X,
  output [15:0] Result_1,
  output Equal,
  output [15:0] Result_2
);

  wire comparator_1_lt;
  wire [15:0] adder_1_out, and_1_out, bit_extender_1_out, multiplier_1_cout, multiplier_1_out, not_1_out,
       or_1_out, or_2_out, shifter_1_out, subtractor_1_out, xor_1_out;

  Shifter #(.width(16)) shifter_1 (.in(X), .\dist (Y[3:0]), .out(shifter_1_out));
  Multiplier #(.width(16)) multiplier_1 (.a(X), .b(Y), .out(multiplier_1_out), .cout(multiplier_1_cout));  // open: cin
  Adder #(.width(16)) adder_1 (.a(X), .b(Y), .out(adder_1_out));  // open: cin, cout
  Subtractor #(.width(16)) subtractor_1 (.a(X), .b(Y), .out(subtractor_1_out));  // open: bin, bout
  assign and_1_out = X & Y;  // AND_Gate and_1, 16 bits wide
  assign or_1_out = X | Y;  // OR_Gate or_1, 16 bits wide
  assign xor_1_out = X ^ Y;  // XOR_Gate xor_1, 16 bits wide
  assign or_2_out = X | Y;  // OR_Gate or_2, 16 bits wide
  Comparator #(.width(16), .mode("unsigned")) comparator_1 (
    .a(X), .b(Y), .eq(Equal), .lt(comparator_1_lt));  // open: gt
  assign not_1_out = ~or_2_out;  // NOT_Gate not_1, 16 bits wide
  assign bit_extender_1_out = {{15{1'b0}}, comparator_1_lt};  // Bit_Extender bit_extender_1
  Multiplexer #(.select(4), .width(16), .enable("false")) multiplexer_1 (
    .in0({16{1'b0}}), .in1({16{1'b0}}), .in2({16{1'b0}}), .in3({16{1'b0}}), .in4({16{1'b0}}),
    .in5(multiplier_1_cout), .in6({16{1'b0}}), .in7({16{1'b0}}), .in8({16{1'b0}}), .in9({16{1'b0}}),
    .in10({16{1'b0}}), .in11({16{1'b0}}), .in12({16{1'b0}}), .in13({16{1'b0}}), .in14({16{1'b0}}),
    .in15({16{1'b0}}), .out(Result_2), .sel(AluOP));
  Multiplexer #(.select(4), .width(16), .enable("false")) multiplexer_2 (
    .in0(shifter_1_out), .in1(multiplier_1_out), .in2(adder_1_out), .in3(subtractor_1_out), .in4(and_1_out),
    .in5(or_1_out), .in6(xor_1_out), .in7(not_1_out), .in8(bit_extender_1_out), .in9({16{1'b0}}),
    .in10({16{1'b0}}), .in11({16{1'b0}}), .in12({16{1'b0}}), .in13({16{1'b0}}), .in14({16{1'b0}}),
    .in15({16{1'b0}}), .out(Result_1), .sel(AluOP));
endmodule

module Op_decoder (
  input  op0,
  input  op1,
  input  op2,
  input  op3,
  output MemRead,
  output MemWrite,
  output ALUSrc,
  output MemtoReg,
  output Branch,
  output RegDst,
  output RegWrite,
  output BneOrBeq,
  output ZeroExtend
);

  wire and_3_out, and_4_out, and_5_out, and_6_out, and_7_out, and_8_out, and_9_out, and_10_out, and_12_out,
       and_13_out, and_15_out, and_16_out, and_17_out, and_18_out, and_19_out, and_20_out, and_21_out,
       and_22_out, and_23_out, and_24_out, and_26_out, and_27_out, not_1_out, not_2_out, not_3_out,
       not_4_out, not_5_out, not_6_out, not_7_out, not_8_out, not_9_out, not_10_out, not_11_out, not_12_out,
       not_13_out, not_14_out, not_15_out, not_16_out, not_17_out, not_18_out, not_19_out, not_20_out,
       not_21_out, not_22_out, not_23_out, not_24_out, not_25_out, not_26_out, not_27_out, not_28_out,
       not_29_out, not_30_out, not_31_out, not_32_out, not_33_out, not_34_out, not_35_out, not_36_out,
       not_37_out, not_38_out, not_39_out, not_40_out, not_41_out, not_42_out, not_43_out, not_44_out,
       not_45_out, not_46_out, not_47_out, not_48_out, not_49_out, not_50_out, not_51_out, not_52_out,
       not_53_out, not_54_out, not_55_out, not_56_out, not_57_out, not_58_out, not_59_out, not_60_out,
       not_61_out, not_62_out, not_63_out, not_64_out, not_65_out, not_66_out, not_67_out, not_68_out,
       not_69_out, not_70_out, not_71_out, not_72_out, not_73_out, not_74_out, not_75_out, not_76_out;

  not not_1 (not_1_out, op1);
  not not_2 (not_2_out, op2);
  not not_3 (not_3_out, op3);
  not not_4 (not_4_out, op1);
  not not_5 (not_5_out, op3);
  not not_6 (not_6_out, op0);
  not not_7 (not_7_out, op1);
  not not_8 (not_8_out, op3);
  not not_9 (not_9_out, op1);
  not not_10 (not_10_out, op2);
  not not_11 (not_11_out, op3);
  not not_12 (not_12_out, op1);
  not not_13 (not_13_out, op3);
  not not_14 (not_14_out, op0);
  not not_15 (not_15_out, op1);
  not not_16 (not_16_out, op0);
  not not_17 (not_17_out, op1);
  not not_18 (not_18_out, op0);
  not not_19 (not_19_out, op1);
  not not_20 (not_20_out, op3);
  not not_21 (not_21_out, op0);
  not not_22 (not_22_out, op1);
  not not_23 (not_23_out, op3);
  not not_24 (not_24_out, op0);
  not not_25 (not_25_out, op1);
  not not_26 (not_26_out, op3);
  not not_27 (not_27_out, op1);
  not not_28 (not_28_out, op2);
  not not_29 (not_29_out, op3);
  not not_30 (not_30_out, op0);
  not not_31 (not_31_out, op1);
  not not_32 (not_32_out, op2);
  not not_33 (not_33_out, op0);
  not not_34 (not_34_out, op1);
  not not_35 (not_35_out, op2);
  not not_36 (not_36_out, op0);
  not not_37 (not_37_out, op1);
  not not_38 (not_38_out, op2);
  not not_39 (not_39_out, op3);
  not not_40 (not_40_out, op0);
  not not_41 (not_41_out, op1);
  not not_42 (not_42_out, op2);
  not not_43 (not_43_out, op3);
  not not_44 (not_44_out, op0);
  not not_45 (not_45_out, op1);
  not not_46 (not_46_out, op3);
  not not_47 (not_47_out, op1);
  not not_48 (not_48_out, op2);
  not not_49 (not_49_out, op3);
  not not_50 (not_50_out, op0);
  not not_51 (not_51_out, op1);
  not not_52 (not_52_out, op0);
  not not_53 (not_53_out, op1);
  not not_54 (not_54_out, op0);
  not not_55 (not_55_out, op1);
  not not_56 (not_56_out, op3);
  not not_57 (not_57_out, op0);
  not not_58 (not_58_out, op1);
  not not_59 (not_59_out, op3);
  not not_60 (not_60_out, op0);
  not not_61 (not_61_out, op1);
  not not_62 (not_62_out, op3);
  not not_63 (not_63_out, op0);
  not not_64 (not_64_out, op1);
  not not_65 (not_65_out, op2);
  not not_66 (not_66_out, op3);
  not not_67 (not_67_out, op0);
  not not_68 (not_68_out, op2);
  not not_69 (not_69_out, op3);
  not not_70 (not_70_out, op0);
  not not_71 (not_71_out, op1);
  not not_72 (not_72_out, op2);
  not not_73 (not_73_out, op0);
  not not_74 (not_74_out, op1);
  not not_75 (not_75_out, op0);
  not not_76 (not_76_out, op1);
  and and_1 (MemRead, op0, not_1_out, not_2_out, not_3_out);
  and and_2 (MemWrite, op0, not_4_out, op2, not_5_out);
  and and_3 (and_3_out, not_6_out, not_7_out, op2, not_8_out);
  and and_4 (and_4_out, op0, not_9_out, not_10_out, not_11_out);
  and and_5 (and_5_out, op0, not_12_out, op2, not_13_out);
  and and_6 (and_6_out, not_14_out, not_15_out, op2, op3);
  and and_7 (and_7_out, not_16_out, not_17_out, op2, op3);
  and and_8 (and_8_out, not_18_out, not_19_out, op2, not_20_out);
  and and_9 (and_9_out, not_21_out, not_22_out, op2, not_23_out);
  and and_10 (and_10_out, not_24_out, not_25_out, op2, not_26_out);
  and and_11 (MemtoReg, op0, not_27_out, not_28_out, not_29_out);
  and and_12 (and_12_out, not_30_out, not_31_out, not_32_out, op3);
  and and_13 (and_13_out, not_33_out, not_34_out, not_35_out, op3);
  and and_14 (RegDst, not_36_out, not_37_out, not_38_out, not_39_out);
  and and_15 (and_15_out, not_40_out, not_41_out, not_42_out, not_43_out);
  and and_16 (and_16_out, not_44_out, not_45_out, op2, not_46_out);
  and and_17 (and_17_out, op0, not_47_out, not_48_out, not_49_out);
  and and_18 (and_18_out, not_50_out, not_51_out, op2, op3);
  and and_19 (and_19_out, not_52_out, not_53_out, op2, op3);
  and and_20 (and_20_out, not_54_out, not_55_out, op2, not_56_out);
  and and_21 (and_21_out, not_57_out, not_58_out, op2, not_59_out);
  and and_22 (and_22_out, not_60_out, not_61_out, op2, not_62_out);
  and and_23 (and_23_out, not_63_out, not_64_out, not_65_out, not_66_out);
  and and_24 (and_24_out, not_67_out, op1, not_68_out, not_69_out);
  and and_25 (BneOrBeq, not_70_out, not_71_out, not_72_out, op3);
  and and_26 (and_26_out, not_73_out, not_74_out, op2, op3);
  and and_27 (and_27_out, not_75_out, not_76_out, op2, op3);
  or or_1 (Branch, and_12_out, and_13_out);
  or or_2 (ALUSrc, and_3_out, and_4_out, and_5_out, and_6_out, and_7_out, and_8_out, and_9_out, and_10_out);
  or or_3 (RegWrite, and_15_out, and_16_out, and_17_out, and_18_out, and_19_out, and_20_out, and_21_out, and_22_out, and_23_out, and_24_out);
  or or_4 (ZeroExtend, and_26_out, and_27_out);
endmodule

module RegRead_detector (
  input  op0,
  input  op1,
  input  op2,
  input  op3,
  output ReadRs,
  output ReadRt
);

  wire and_1_out, and_2_out, and_3_out, and_4_out, and_5_out, and_6_out, and_7_out, and_8_out, and_9_out,
       and_10_out, and_11_out, and_12_out, and_13_out, and_14_out, and_15_out, not_1_out, not_2_out,
       not_3_out, not_4_out, not_5_out, not_6_out, not_7_out, not_8_out, not_9_out, not_10_out, not_11_out,
       not_12_out, not_13_out, not_14_out, not_15_out, not_16_out, not_17_out, not_18_out, not_19_out,
       not_20_out, not_21_out, not_22_out, not_23_out, not_24_out, not_25_out, not_26_out, not_27_out,
       not_28_out, not_29_out, not_30_out, not_31_out, not_32_out, not_33_out, not_34_out, not_35_out,
       not_36_out, not_37_out, not_38_out, not_39_out, not_40_out, not_41_out, not_42_out;

  not not_1 (not_1_out, op0);
  not not_2 (not_2_out, op1);
  not not_3 (not_3_out, op2);
  not not_4 (not_4_out, op3);
  not not_5 (not_5_out, op0);
  not not_6 (not_6_out, op1);
  not not_7 (not_7_out, op3);
  not not_8 (not_8_out, op0);
  not not_9 (not_9_out, op1);
  not not_10 (not_10_out, op3);
  not not_11 (not_11_out, op0);
  not not_12 (not_12_out, op1);
  not not_13 (not_13_out, op0);
  not not_14 (not_14_out, op1);
  not not_15 (not_15_out, op1);
  not not_16 (not_16_out, op2);
  not not_17 (not_17_out, op3);
  not not_18 (not_18_out, op0);
  not not_19 (not_19_out, op1);
  not not_20 (not_20_out, op2);
  not not_21 (not_21_out, op0);
  not not_22 (not_22_out, op1);
  not not_23 (not_23_out, op2);
  not not_24 (not_24_out, op0);
  not not_25 (not_25_out, op1);
  not not_26 (not_26_out, op3);
  not not_27 (not_27_out, op1);
  not not_28 (not_28_out, op3);
  not not_29 (not_29_out, op0);
  not not_30 (not_30_out, op1);
  not not_31 (not_31_out, op2);
  not not_32 (not_32_out, op0);
  not not_33 (not_33_out, op1);
  not not_34 (not_34_out, op2);
  not not_35 (not_35_out, op0);
  not not_36 (not_36_out, op1);
  not not_37 (not_37_out, op2);
  not not_38 (not_38_out, op0);
  not not_39 (not_39_out, op2);
  not not_40 (not_40_out, op3);
  not not_41 (not_41_out, op1);
  not not_42 (not_42_out, op3);
  and and_1 (and_1_out, not_1_out, not_2_out, not_3_out, not_4_out);
  and and_2 (and_2_out, not_5_out, not_6_out, op2, not_7_out);
  and and_3 (and_3_out, not_8_out, not_9_out, op2, not_10_out);
  and and_4 (and_4_out, not_11_out, not_12_out, op2, op3);
  and and_5 (and_5_out, not_13_out, not_14_out, op2, op3);
  and and_6 (and_6_out, op0, not_15_out, not_16_out, not_17_out);
  and and_7 (and_7_out, not_18_out, not_19_out, not_20_out, op3);
  and and_8 (and_8_out, not_21_out, not_22_out, not_23_out, op3);
  and and_9 (and_9_out, not_24_out, not_25_out, op2, not_26_out);
  and and_10 (and_10_out, op0, not_27_out, op2, not_28_out);
  and and_11 (and_11_out, not_29_out, not_30_out, not_31_out, op3);
  and and_12 (and_12_out, not_32_out, not_33_out, not_34_out, op3);
  and and_13 (and_13_out, not_35_out, not_36_out, not_37_out, op3);
  and and_14 (and_14_out, not_38_out, op1, not_39_out, not_40_out);
  and and_15 (and_15_out, op0, not_41_out, op2, not_42_out);
  or or_1 (ReadRs, and_1_out, and_2_out, and_3_out, and_4_out, and_5_out, and_6_out, and_7_out, and_8_out, and_9_out, and_10_out);
  or or_2 (ReadRt, and_11_out, and_12_out, and_13_out, and_14_out, and_15_out);
endmodule

module Extender_immediate (
  input  ZeroExtend,
  input  [7:0] Input,
  output [15:0] Output
);

  wire [15:0] bit_extender_1_out, bit_extender_2_out;

  assign bit_extender_1_out = {{8{Input[7]}}, Input};  // Bit_Extender bit_extender_1
  assign bit_extender_2_out = {{8{1'b0}}, Input};  // Bit_Extender bit_extender_2
  Multiplexer #(.width(16), .enable("false")) multiplexer_1 (
    .in0(bit_extender_1_out), .in1(bit_extender_2_out), .out(Output), .sel(ZeroExtend));
endmodule

module Control (
  input  [3:0] op,
  output MemRead,
  output MemWrite,
  output ALUSrc,
  output MemtoReg,
  output Branch,
  output RegDst,
  output RegWrite,
  output BneOrBeq,
  output ZeroExtend,
  output ReadRs,
  output ReadRt
);

  Op_decoder op_decoder_1 (
    .op0(op[3]), .op1(op[2]), .op2(op[1]), .op3(op[0]), .MemRead(MemRead), .MemWrite(MemWrite),
    .ALUSrc(ALUSrc), .MemtoReg(MemtoReg), .Branch(Branch), .RegDst(RegDst), .RegWrite(RegWrite),
    .BneOrBeq(BneOrBeq), .ZeroExtend(ZeroExtend));
  RegRead_detector regread_detector_1 (
    .op0(op[3]), .op1(op[2]), .op2(op[1]), .op3(op[0]), .ReadRs(ReadRs), .ReadRt(ReadRt));
endmodule

module RegFile (
  input  [3:0] R1_num,
  input  WE,
  input  [3:0] R2_num,
  input  clk,
  input  [3:0] RW,
  input  [15:0] Din,
  output [15:0] R1,
  output [15:0] R2
);

  wire demultiplexer_1_out0, demultiplexer_1_out1, demultiplexer_2_out0, demultiplexer_2_out1,
       demultiplexer_2_out2, demultiplexer_2_out3, demultiplexer_2_out4, demultiplexer_2_out5,
       demultiplexer_2_out6, demultiplexer_2_out7, demultiplexer_3_out0, demultiplexer_3_out1,
       demultiplexer_3_out2, demultiplexer_3_out3, demultiplexer_3_out4, demultiplexer_3_out5,
       demultiplexer_3_out6, demultiplexer_3_out7;
  wire [15:0] _0__Zero_q, _1__v0_q, _2__v1_q, _3__t0_q, _4__t1_q, _5__t2_q, _6__t3_q, _7__t4_q, _8__t5_q,
       _9__t6_q, _10__t7_q, _14__s4_q, _15__s5_q, s0, s1, s2;

  Demultiplexer #(.disabled(0)) demultiplexer_1 (
    .out0(demultiplexer_1_out0), .out1(demultiplexer_1_out1), .in(1'b1), .sel(RW[3]), .en(WE));
  Demultiplexer #(.select(3), .disabled(0)) demultiplexer_2 (
    .out0(demultiplexer_2_out0), .out1(demultiplexer_2_out1), .out2(demultiplexer_2_out2),
    .out3(demultiplexer_2_out3), .out4(demultiplexer_2_out4), .out5(demultiplexer_2_out5),
    .out6(demultiplexer_2_out6), .out7(demultiplexer_2_out7), .in(1'b1), .sel(RW[2:0]),
    .en(demultiplexer_1_out0));
  Demultiplexer #(.select(3), .disabled(0)) demultiplexer_3 (
    .out0(demultiplexer_3_out0), .out1(demultiplexer_3_out1), .out2(demultiplexer_3_out2),
    .out3(demultiplexer_3_out3), .out4(demultiplexer_3_out4), .out5(demultiplexer_3_out5),
    .out6(demultiplexer_3_out6), .out7(demultiplexer_3_out7), .in(1'b1), .sel(RW[2:0]),
    .en(demultiplexer_1_out1));
  Register #(.width(16)) _0__Zero (.D(Din), .en(demultiplexer_2_out0), .Q(_0__Zero_q));  // open: clk, clr
  Register #(.width(16)) _8__t5 (.D(Din), .en(demultiplexer_3_out0), .Q(_8__t5_q), .clk(clk));  // open: clr
  Register #(.width(16)) _1__v0 (.D(Din), .en(demultiplexer_2_out1), .Q(_1__v0_q), .clk(clk));  // open: clr
  Register #(.width(16)) _9__t6 (.D(Din), .en(demultiplexer_3_out1), .Q(_9__t6_q), .clk(clk));  // open: clr
  Register #(.width(16)) _2__v1 (.D(Din), .en(demultiplexer_2_out2), .Q(_2__v1_q), .clk(clk));  // open: clr
  Register #(.width(16)) _10__t7 (.D(Din), .en(demultiplexer_3_out2), .Q(_10__t7_q), .clk(clk));  // open: clr
  Register #(.width(16)) _3__t0 (.D(Din), .en(demultiplexer_2_out3), .Q(_3__t0_q), .clk(clk));  // open: clr
  Register #(.width(16)) _11__s0 (.D(Din), .en(demultiplexer_3_out3), .Q(s0), .clk(clk));  // open: clr
  Register #(.width(16)) _4__t1 (.D(Din), .en(demultiplexer_2_out4), .Q(_4__t1_q), .clk(clk));  // open: clr
  Register #(.width(16)) _12__s1 (.D(Din), .en(demultiplexer_3_out4), .Q(s1), .clk(clk));  // open: clr
  Register #(.width(16)) _5__t2 (.D(Din), .en(demultiplexer_2_out5), .Q(_5__t2_q), .clk(clk));  // open: clr
  Register #(.width(16)) _13__s3 (.D(Din), .en(demultiplexer_3_out5), .Q(s2), .clk(clk));  // open: clr
  Register #(.width(16)) _6__t3 (.D(Din), .en(demultiplexer_2_out6), .Q(_6__t3_q), .clk(clk));  // open: clr
  Register #(.width(16)) _14__s4 (.D(Din), .en(demultiplexer_3_out6), .Q(_14__s4_q), .clk(clk));  // open: clr
  Register #(.width(16)) _7__t4 (.D(Din), .en(demultiplexer_2_out7), .Q(_7__t4_q), .clk(clk));  // open: clr
  Register #(.width(16)) _15__s5 (.D(Din), .en(demultiplexer_3_out7), .Q(_15__s5_q), .clk(clk));  // open: clr
  Multiplexer #(.select(4), .width(16), .enable("false")) multiplexer_1 (
    .in0(_0__Zero_q), .in1(_1__v0_q), .in2(_2__v1_q), .in3(_3__t0_q), .in4(_4__t1_q), .in5(_5__t2_q),
    .in6(_6__t3_q), .in7(_7__t4_q), .in8(_8__t5_q), .in9(_9__t6_q), .in10(_10__t7_q), .in11(s0), .in12(s1),
    .in13(s2), .in14(_14__s4_q), .in15(_15__s5_q), .out(R1), .sel(R1_num));
  Multiplexer #(.select(4), .width(16), .enable("false")) multiplexer_2 (
    .in0(_0__Zero_q), .in1(_1__v0_q), .in2(_2__v1_q), .in3(_3__t0_q), .in4(_4__t1_q), .in5(_5__t2_q),
    .in6(_6__t3_q), .in7(_7__t4_q), .in8(_8__t5_q), .in9(_9__t6_q), .in10(_10__t7_q), .in11(s0), .in12(s1),
    .in13(s2), .in14(_14__s4_q), .in15(_15__s5_q), .out(R2), .sel(R2_num));

  // Other names for the same wires on the sheet: reg1[15:0] = R1; reg1_num[3:0] = R1_num; reg2[15:0] = R2;
  //   reg2_num[3:0] = R2_num; write_data[15:0] = Din; write_reg_num[3:0] = RW
endmodule

module pipeline_IF_ID (
  input  En,
  input  [15:0] InstIF,
  input  clk,
  input  clr,
  input  [15:0] PCPlus4ID,
  output [15:0] InstID,
  output [15:0] PCPlus4IF
);

  Register #(.width(16)) register_1 (.D(InstIF), .en(En), .Q(InstID), .clk(clk), .clr(clr));
  Register #(.width(16)) register_2 (.D(PCPlus4ID), .en(En), .Q(PCPlus4IF), .clk(clk), .clr(clr));
endmodule

module pipeline_ID_EX (
  input  clk,
  input  clr,
  input  En,
  input  MemReadID,
  input  [15:0] ImmID,
  input  MemWriteID,
  input  [15:0] R1ID,
  input  ALUSrcID,
  input  [15:0] R2ID,
  input  MemtoRegID,
  input  [15:0] PCPlus4ID,
  input  BranchID,
  input  [3:0] WriteRegID,
  input  RegWriteID,
  input  BneOrBeqID,
  output MemReadEX,
  output [15:0] ImmEX,
  output MemWriteEX,
  output [15:0] R1EX,
  output ALUSrcEX,
  output [15:0] R2EX,
  output MemtoRegEX,
  output [15:0] PCPlusEX,
  output BranchEX,
  output [3:0] WriteRegEX,
  output RegWriteEX,
  output BneOrBeqEX
);

  Register #(.width(1)) register_1 (.D(MemReadID), .en(En), .Q(MemReadEX), .clk(clk), .clr(clk));
  Register #(.width(1)) register_2 (.D(MemWriteID), .Q(MemWriteEX), .clk(clk), .clr(clk));  // open: en
  Register #(.width(1)) register_3 (.D(ALUSrcID), .en(En), .Q(ALUSrcEX), .clk(clk), .clr(clk));
  Register #(.width(1)) register_4 (.D(MemtoRegID), .en(En), .Q(MemtoRegEX), .clk(clk), .clr(clk));
  Register #(.width(1)) register_5 (.D(BranchID), .en(En), .Q(BranchEX), .clk(clk), .clr(clk));
  Register #(.width(1)) register_6 (.D(RegWriteID), .en(En), .Q(RegWriteEX), .clk(clk), .clr(clk));
  Register #(.width(1)) register_7 (.D(BneOrBeqID), .en(En), .Q(BneOrBeqEX), .clk(clk), .clr(clk));
  Register #(.width(16)) register_8 (.D(ImmID), .en(En), .Q(ImmEX), .clk(clk), .clr(clr));
  Register #(.width(16)) register_9 (.D(R1ID), .en(En), .Q(R1EX), .clk(clk), .clr(clr));
  Register #(.width(16)) register_10 (.D(R2ID), .en(En), .Q(R2EX), .clk(clk), .clr(clr));
  Register #(.width(16)) register_11 (.D(PCPlus4ID), .en(En), .Q(PCPlusEX), .clk(clk), .clr(clr));
  Register #(.width(4)) register_12 (.D(WriteRegID), .en(En), .Q(WriteRegEX), .clk(clk), .clr(clr));
endmodule

module pipeline_EX_MEM (
  input  clk,
  input  clr,
  input  En,
  input  MemReadEX,
  input  [15:0] ALUResultEX,
  input  MemWriteEX,
  input  [15:0] WriteDataEX,
  input  MemtoRegEX,
  input  RegWriteEX,
  input  [3:0] WriteRegEX,
  output MemReadMEM,
  output [15:0] ALUResultMEM,
  output MemWriteMEM,
  output [15:0] WriteDataMEM,
  output MemtoRegMEM,
  output RegWriteMEM,
  output [3:0] WriteRegMEM
);

  Register #(.width(1)) register_1 (.D(MemReadEX), .en(En), .Q(MemReadMEM), .clk(clk), .clr(clr));
  Register #(.width(1)) register_2 (.D(MemWriteEX), .en(En), .Q(MemWriteMEM), .clk(clk), .clr(clr));
  Register #(.width(1)) register_3 (.D(MemtoRegEX), .en(En), .Q(MemtoRegMEM), .clk(clk), .clr(clr));
  Register #(.width(1)) register_4 (.D(RegWriteEX), .en(En), .Q(RegWriteMEM), .clk(clk), .clr(clr));
  Register #(.width(4)) register_5 (.D(WriteRegEX), .en(En), .Q(WriteRegMEM), .clk(clk), .clr(clr));
  Register #(.width(16)) register_6 (.D(ALUResultEX), .en(En), .Q(ALUResultMEM), .clk(clk), .clr(clr));
  Register #(.width(16)) register_7 (.D(WriteDataEX), .en(En), .Q(WriteDataMEM), .clk(clk), .clr(clr));
endmodule

module pipeline_MEM_WB (
  input  clk,
  input  clr,
  input  En,
  input  RegWriteMEM,
  input  [15:0] ALUResultMEM,
  input  MemtoRegMEM,
  input  [15:0] ReadDataMEM,
  input  [3:0] WriteRegMEM,
  input  [15:0] JumpAddrMEM,
  output RegWriteWB,
  output [15:0] ALUResultWB,
  output MemtoRegWB,
  output [15:0] ReadDataWB,
  output [3:0] WriteRegWB,
  output [15:0] JumpAddrWB
);

  Register #(.width(1)) register_1 (.D(RegWriteMEM), .en(En), .Q(RegWriteWB), .clk(clk), .clr(clr));
  Register #(.width(1)) register_2 (.D(MemtoRegMEM), .en(En), .Q(MemtoRegWB), .clk(clk), .clr(clr));
  Register #(.width(4)) register_3 (.D(WriteRegMEM), .en(En), .Q(WriteRegWB), .clk(clk), .clr(clr));
  Register #(.width(16)) register_4 (.D(ALUResultMEM), .en(En), .Q(ALUResultWB), .clk(clk), .clr(clr));
  Register #(.width(16)) register_5 (.D(ReadDataMEM), .en(En), .Q(ReadDataWB), .clk(clk), .clr(clr));
  Register #(.width(16)) register_6 (.D(JumpAddrMEM), .en(En), .Q(JumpAddrWB), .clk(clk), .clr(clr));
endmodule
